// Logisim project ex4.circ as structural Verilog: 5 circuits, main circuit RotRight
module RotRight (
  input  [15:0] INPUT0,
  input  [3:0] AMOUNT,
  output [15:0] OUTPUT0
);

  wire [15:0] multiplexer_1_out, multiplexer_2_out, multiplexer_3_out, rot1_1_out_2, rot2_1_out_2,
       rot4_1_out_2, rot8_1_out_2;

  rot1 rot1_1 (.out_2(rot1_1_out_2), .in_1(INPUT0));
  Multiplexer #(.enable("false"), .width(16)) multiplexer_1 (
    .in0(INPUT0), .in1(rot1_1_out_2), .out(multiplexer_1_out), .sel(AMOUNT[0]));
  rot2 rot2_1 (.out_2(rot2_1_out_2), .in_1(multiplexer_1_out));
  Multiplexer #(.enable("false"), .width(16)) multiplexer_2 (
    .in0(multiplexer_1_out), .in1(rot2_1_out_2), .out(multiplexer_2_out), .sel(AMOUNT[1]));
  Multiplexer #(.enable("false"), .width(16)) multiplexer_3 (
    .in0(multiplexer_2_out), .in1(rot4_1_out_2), .out(multiplexer_3_out), .sel(AMOUNT[2]));
  rot4 rot4_1 (.out_2(rot4_1_out_2), .in_1(multiplexer_2_out));
  Multiplexer #(.enable("false"), .width(16)) multiplexer_4 (
    .in0(multiplexer_3_out), .in1(rot8_1_out_2), .out(OUTPUT0), .sel(AMOUNT[3]));
  rot8 rot8_1 (.out_2(rot8_1_out_2), .in_1(multiplexer_3_out));

  // Other names for the same wires on the sheet: bit0 = AMOUNT[0]; bit1 = AMOUNT[1]; bit2 = AMOUNT[2];
  //   bit3 = AMOUNT[3]
endmodule

module rot1 (
  input  [15:0] in_1,
  output [15:0] out_2
);

  wire [15:0] bit_extender_1_out, multiplexer_1_out;

  Multiplexer #(.enable("false"), .width(16)) multiplexer_1 (
    .in0({16{1'b0}}), .in1(16'h8000), .out(multiplexer_1_out), .sel(in_1[0]));
  assign bit_extender_1_out = {{1{1'b0}}, in_1[15:1]};  // Bit_Extender bit_extender_1
  assign out_2 = multiplexer_1_out | bit_extender_1_out;  // OR_Gate or_1, 16 bits wide
endmodule

module rot2 (
  input  [15:0] in_1,
  output [15:0] out_2
);

  wire [15:0] bit_extender_1_out, multiplexer_1_out;

  Multiplexer #(.enable("false"), .select(2), .width(16)) multiplexer_1 (
    .in0({16{1'b0}}), .in1(16'h4000), .in2(16'h8000), .in3(16'hc000), .out(multiplexer_1_out), .sel(in_1[1:0]));
  assign bit_extender_1_out = {{2{1'b0}}, in_1[15:2]};  // Bit_Extender bit_extender_1
  assign out_2 = multiplexer_1_out | bit_extender_1_out;  // OR_Gate or_1, 16 bits wide
endmodule

module rot4 (
  input  [15:0] in_1,
  output [15:0] out_2
);

  wire [12:0] bit_extender_1_out;
  wire [13:0] bit_extender_2_out;
  wire [14:0] bit_extender_3_out;

  assign bit_extender_1_out = {{1{in_1[0]}}, in_1[15:4]};  // Bit_Extender bit_extender_1
  assign bit_extender_2_out = {{1{in_1[1]}}, bit_extender_1_out};  // Bit_Extender bit_extender_2
  assign bit_extender_3_out = {{1{in_1[2]}}, bit_extender_2_out};  // Bit_Extender bit_extender_3
  assign out_2 = {{1{in_1[3]}}, bit_extender_3_out};  // Bit_Extender bit_extender_4

  // Other names for the same wires on the sheet: bit0 = in_1[0]; bit1 = in_1[1]; bit2 = in_1[2]; bit3 = in_1[3]
endmodule

module rot8 (
  input  [15:0] in_1,
  output [15:0] out_2
);


  assign out_2 = {in_1[7:0], in_1[15:8]};
endmodule
