// Logisim project control-logic.circ as structural Verilog: 1 circuit, main circuit control_logic
module control_logic (
  input  [31:0] inst,
  input  BrEq,
  input  BrLt,
  output PCSel,
  output RegWEn,
  output [2:0] ImmSel,
  output BrUn,
  output ASel,
  output BSel,
  output [3:0] ALUSel,
  output MemRW,
  output [1:0] WBSel,
  output CSRSel,
  output CSRWen
);

  wire AddSel, and_1_out, and_13_out, and_14_out, and_16_out, and_17_out, and_18_out, and_19_out, and_20_out,
       and_21_out, and_22_out, AndSel, ArimeticCal, comp_Result, comparator_2_eq, comparator_3_eq,
       comparator_6_eq, comparator_7_eq, comparator_10_eq, comparator_11_eq, comparator_12_eq,
       comparator_13_eq, comparator_14_eq, comparator_15_eq, comparator_16_eq, comparator_17_eq,
       comparator_19_eq, comparator_20_eq, comparator_21_eq, comparator_22_eq, comparator_23_eq,
       comparator_24_eq, comparator_25_eq, comparator_26_eq, comparator_27_eq, comparator_28_eq,
       comparator_30_eq, comparator_31_eq, funct3_000, funct3_001, funct3_002, funct3_003, funct3_004,
       funct3_005, funct3_006, funct3_007, funct7_00, I_type, jump, MulhSel, MulhuSel, MulSel, not_1_out,
       not_2_out, not_3_out, not_4_out, not_5_out, not_6_out, or_5_out, or_10_out, OrSel, R_I_ALU_Type,
       R_Type, R_type_t, S_type, SB_type, SllSel, SltSel, SraSel, SrlSel, SubSel, U_type, UJ_type, WB_is0,
       WB_is1, WB_is2, XorSel;

  Comparator #(.mode("unsigned"), .width(7)) comparator_1 (
    .a(inst[6:0]), .b(7'b0110011), .eq(R_type_t));  // open: gt, lt
  Comparator #(.mode("unsigned"), .width(7)) comparator_2 (
    .a(inst[6:0]), .b(7'b0000011), .eq(comparator_2_eq));  // open: gt, lt
  Comparator #(.mode("unsigned"), .width(7)) comparator_3 (
    .a(inst[6:0]), .b(7'b0010011), .eq(comparator_3_eq));  // open: gt, lt
  Comparator #(.mode("unsigned"), .width(7)) comparator_4 (.a(inst[6:0]), .b(7'b0100011), .eq(S_type));  // open: gt, lt
  Comparator #(.mode("unsigned"), .width(7)) comparator_5 (
    .a(inst[6:0]), .b(7'b1100011), .eq(SB_type));  // open: gt, lt
  Comparator #(.mode("unsigned"), .width(7)) comparator_6 (
    .a(inst[6:0]), .b(7'b0010111), .eq(comparator_6_eq));  // open: gt, lt
  Comparator #(.mode("unsigned"), .width(7)) comparator_7 (
    .a(inst[6:0]), .b(7'b0110111), .eq(comparator_7_eq));  // open: gt, lt
  Comparator #(.mode("unsigned"), .width(7)) comparator_8 (
    .a(inst[6:0]), .b(7'b1101111), .eq(UJ_type));  // open: gt, lt
  Comparator #(.mode("unsigned"), .width(7)) comparator_9 (.a(inst[6:0]), .b(7'b1110011), .eq(CSRSel));  // open: gt, lt
  or or_1 (ArimeticCal, comparator_2_eq, comparator_3_eq);
  or or_2 (U_type, comparator_6_eq, comparator_7_eq);
  Comparator #(.mode("unsigned"), .width(7)) comparator_10 (
    .a(inst[6:0]), .b(7'b0010011), .eq(comparator_10_eq));  // open: gt, lt
  Comparator #(.mode("unsigned"), .width(7)) comparator_11 (
    .a(inst[6:0]), .b(7'b0110011), .eq(comparator_11_eq));  // open: gt, lt
  or or_3 (RegWEn, R_type_t, ArimeticCal, U_type, jump);
  Priority_Encoder priority_encoder_1 (
    .in0(I_type), .in1(S_type), .in2(SB_type), .in3(U_type), .in4(UJ_type), .in5(1'b0), .in6(1'b0),
    .in7(1'b0), .out(ImmSel));  // open: en_in, gs, en_out
  Comparator #(.mode("unsigned"), .width(7)) comparator_12 (
    .a(inst[6:0]), .b(7'b0000011), .eq(comparator_12_eq));  // open: gt, lt
  Comparator #(.mode("unsigned"), .width(7)) comparator_13 (
    .a(inst[6:0]), .b(7'b0100011), .eq(comparator_13_eq));  // open: gt, lt
  Comparator #(.mode("unsigned"), .width(7)) comparator_14 (
    .a(inst[6:0]), .b(7'b1100011), .eq(comparator_14_eq));  // open: gt, lt
  Comparator #(.mode("unsigned"), .width(7)) comparator_15 (
    .a(inst[6:0]), .b(7'b0010111), .eq(comparator_15_eq));  // open: gt, lt
  Comparator #(.mode("unsigned"), .width(7)) comparator_16 (
    .a(inst[6:0]), .b(7'b1101111), .eq(comparator_16_eq));  // open: gt, lt
  and and_1 (and_1_out, R_type_t, funct3_000, funct7_00);
  and and_2 (SubSel, R_type_t, funct3_000, inst[30]);
  Comparator #(.mode("unsigned"), .width(7)) comparator_17 (
    .a(inst[6:0]), .b(7'b1100111), .eq(comparator_17_eq));  // open: gt, lt
  or or_4 (R_I_ALU_Type, comparator_10_eq, comparator_11_eq);
  and and_3 (SllSel, R_I_ALU_Type, funct3_001);
  and and_4 (XorSel, R_I_ALU_Type, funct3_004);
  and and_5 (SrlSel, R_I_ALU_Type, funct3_005, funct7_00);
  and and_6 (SraSel, R_I_ALU_Type, funct3_005, inst[30]);
  and and_7 (OrSel, R_I_ALU_Type, funct3_006);
  and and_8 (AndSel, R_I_ALU_Type, funct3_007);
  and and_9 (MulhuSel, R_Type, funct3_003, inst[25]);
  and and_10 (MulSel, R_Type, funct3_000, inst[25]);
  and and_11 (MulhSel, R_Type, funct3_001, inst[25]);
  and and_12 (SltSel, R_I_ALU_Type, funct3_002);
  Comparator #(.mode("unsigned"), .width(7)) comparator_18 (.a(inst[6:0]), .b(7'b0100011), .eq(MemRW));  // open: gt, lt
  or or_5 (or_5_out, ArimeticCal, comparator_17_eq);
  or or_6 (jump, comparator_17_eq, UJ_type);
  or or_7 (AddSel, comparator_12_eq, comparator_13_eq, comparator_14_eq, comparator_15_eq, comparator_16_eq, and_1_out);
  Comparator #(.mode("unsigned"), .width(7)) comparator_19 (
    .a(inst[6:0]), .b(7'b1110011), .eq(comparator_19_eq));  // open: gt, lt
  Comparator #(.mode("unsigned"), .width(3)) comparator_20 (
    .a(inst[14:12]), .b(3'b101), .eq(comparator_20_eq));  // open: gt, lt
  or or_8 (BSel, R_type_t, S_type, SB_type);
  or or_9 (I_type, or_5_out, comparator_19_eq);
  and and_13 (and_13_out, CSRSel, comparator_20_eq);
  not not_1 (not_1_out, and_13_out);
  Comparator #(.mode("unsigned"), .width(3)) comparator_21 (
    .a(inst[14:12]), .b(3'b110), .eq(comparator_21_eq));  // open: gt, lt
  Comparator #(.mode("unsigned"), .width(3)) comparator_22 (
    .a(inst[14:12]), .b(3'b111), .eq(comparator_22_eq));  // open: gt, lt
  or or_10 (or_10_out, comparator_21_eq, comparator_22_eq);
  and and_14 (and_14_out, I_type, not_1_out);
  Priority_Encoder #(.select(4)) priority_encoder_2 (
    .in0(AddSel), .in1(SllSel), .in2(SltSel), .in4(XorSel), .in5(SrlSel), .in6(OrSel), .in7(AndSel),
    .in8(MulSel), .in9(MulhSel), .in11(MulhuSel), .in12(SubSel), .in13(SraSel), .in15(BSel), .out(ALUSel));  // open: in3, in10, in14, gs, en_out, en_in
  and and_15 (BrUn, SB_type, or_10_out);
  Comparator #(.mode("unsigned"), .width(3)) comparator_23 (
    .a(inst[14:12]), .b(3'b000), .eq(comparator_23_eq));  // open: gt, lt
  Comparator #(.mode("unsigned"), .width(3)) comparator_24 (
    .a(inst[14:12]), .b(3'b001), .eq(comparator_24_eq));  // open: gt, lt
  not not_2 (not_2_out, BrEq);
  Comparator #(.mode("unsigned"), .width(3)) comparator_25 (
    .a(inst[14:12]), .b(3'b100), .eq(comparator_25_eq));  // open: gt, lt
  Comparator #(.mode("unsigned"), .width(3)) comparator_26 (
    .a(inst[14:12]), .b(3'b101), .eq(comparator_26_eq));  // open: gt, lt
  not not_3 (not_3_out, BrLt);
  Comparator #(.mode("unsigned"), .width(3)) comparator_27 (
    .a(inst[14:12]), .b(3'b110), .eq(comparator_27_eq));  // open: gt, lt
  Comparator #(.mode("unsigned"), .width(3)) comparator_28 (
    .a(inst[14:12]), .b(3'b111), .eq(comparator_28_eq));  // open: gt, lt
  not not_4 (not_4_out, BrLt);
  or or_11 (ASel, R_type_t, and_14_out, S_type, SB_type);
  and and_16 (and_16_out, comparator_23_eq, BrEq);
  and and_17 (and_17_out, comparator_24_eq, not_2_out);
  and and_18 (and_18_out, comparator_25_eq, BrLt);
  and and_19 (and_19_out, comparator_26_eq, not_3_out);
  and and_20 (and_20_out, comparator_27_eq, BrLt);
  and and_21 (and_21_out, comparator_28_eq, not_4_out);
  and and_22 (and_22_out, comp_Result, SB_type);
  or or_12 (PCSel, and_22_out, jump);
  or or_13 (comp_Result, and_16_out, and_17_out, and_18_out, and_19_out, and_20_out, and_21_out);
  Decoder #(.select(3)) decoder_1 (
    .out0(funct3_000), .out1(funct3_001), .out2(funct3_002), .out3(funct3_003), .out4(funct3_004),
    .out5(funct3_005), .out6(funct3_006), .out7(funct3_007), .sel(inst[14:12]));  // open: en
  Comparator #(.mode("unsigned"), .width(7)) comparator_29 (
    .a(inst[31:25]), .b({7{1'b0}}), .eq(funct7_00));  // open: gt, lt
  not not_5 (not_5_out, WB_is2);
  not not_6 (not_6_out, WB_is1);
  Comparator #(.mode("unsigned"), .width(7)) comparator_30 (
    .a(inst[6:0]), .b(7'b0010011), .eq(comparator_30_eq));  // open: gt, lt
  Comparator #(.mode("unsigned"), .width(7)) comparator_31 (
    .a(inst[6:0]), .b(7'b0000011), .eq(comparator_31_eq));  // open: gt, lt
  Priority_Encoder #(.select(2)) priority_encoder_3 (
    .in0(WB_is0), .in1(WB_is1), .in2(WB_is2), .out(WBSel));  // open: in3, gs, en_out, en_in
  or or_14 (WB_is0, not_5_out, not_6_out, R_type_t, comparator_30_eq);
  or or_15 (WB_is1, S_type, comparator_31_eq);
  or or_16 (WB_is2, U_type, UJ_type);

  assign CSRWen = CSRSel;

  // Other names for the same wires on the sheet: csrw = CSRSel; opcode[6:0] = inst[6:0]; funct3[2:0] = inst[14:12];
  //   funct7[6:0] = inst[31:25]; funct7_01 = inst[25]; funct7_20 = inst[30]

  // Notes on the sheet:
  //   INPUTS to your circuit
  //   DON'T CHANGE THE LOCATIONS OF THE INPUTS AND OUTPUTS!
  //   OUTPUT from your circuit
  //   csrwi
endmodule
