// Logisim project regfile.circ as structural Verilog: 1 circuit, main circuit regfile
module regfile (
  input  [4:0] rs1,
  input  [4:0] rs2,
  input  [4:0] rd,
  input  [31:0] Write_Data,
  input  RegWEn,
  input  clk,
  output [31:0] ra,
  output [31:0] sp,
  output [31:0] t0,
  output [31:0] t1,
  output [31:0] t2,
  output [31:0] s0,
  output [31:0] s1,
  output [31:0] a0,
  output [31:0] Read_Data_1,
  output [31:0] Read_Data_2
);

  wire and_1_out, and_2_out, and_3_out, and_4_out, and_5_out, and_6_out, and_7_out, and_8_out, and_9_out,
       and_10_out, and_11_out, and_12_out, and_13_out, and_14_out, and_15_out, and_16_out, and_17_out,
       and_18_out, and_19_out, and_20_out, and_21_out, and_22_out, and_23_out, and_24_out, and_25_out,
       and_26_out, and_27_out, and_28_out, and_29_out, and_30_out, and_31_out, wreg1, wreg2, wreg3, wreg4,
       wreg5, wreg6, wreg7, wreg8, wreg9, wreg10, wreg11, wreg13, wreg14, wreg15, wreg16, wreg17, wreg18,
       wreg19, wreg20, wreg21, wreg22, wreg23, wreg24, wreg25, wreg26, wreg27, wreg28, wreg29, wreg30, wreg31;
  wire [31:0] rg4, rg5, rg12, rg13, rg14, rg15, rg16, rg17, rg18, rg19, rg20, rg21, rg22, rg23, rg24, rg25,
       rg26, rg27, rg28, rg29, rg30, rg31, rg32, undriven;

  Decoder #(.enable("false"), .select(5)) decoder_1 (
    .out1(wreg1), .out2(wreg2), .out3(wreg3), .out4(wreg4), .out5(wreg5), .out6(wreg6), .out7(wreg7),
    .out8(wreg8), .out9(wreg9), .out10(wreg10), .out11(wreg11), .out12(wreg11), .out13(wreg13),
    .out14(wreg14), .out15(wreg15), .out16(wreg16), .out17(wreg17), .out18(wreg18), .out19(wreg19),
    .out20(wreg20), .out21(wreg21), .out22(wreg22), .out23(wreg23), .out24(wreg24), .out25(wreg25),
    .out26(wreg26), .out27(wreg27), .out28(wreg28), .out29(wreg29), .out30(wreg30), .out31(wreg31), .sel(rd));  // open: out0
  and and_1 (and_1_out, wreg1, RegWEn);
  and and_2 (and_2_out, wreg2, RegWEn);
  and and_3 (and_3_out, wreg3, RegWEn);
  and and_4 (and_4_out, wreg4, RegWEn);
  and and_5 (and_5_out, wreg5, RegWEn);
  and and_6 (and_6_out, wreg6, RegWEn);
  and and_7 (and_7_out, wreg7, RegWEn);
  and and_8 (and_8_out, wreg8, RegWEn);
  and and_9 (and_9_out, wreg9, RegWEn);
  and and_10 (and_10_out, wreg10, RegWEn);
  and and_11 (and_11_out, wreg11, RegWEn);
  and and_12 (and_12_out, wreg11, RegWEn);
  and and_13 (and_13_out, wreg13, RegWEn);
  and and_14 (and_14_out, wreg14, RegWEn);
  and and_15 (and_15_out, wreg15, RegWEn);
  and and_16 (and_16_out, wreg16, RegWEn);
  and and_17 (and_17_out, wreg17, RegWEn);
  and and_18 (and_18_out, wreg18, RegWEn);
  and and_19 (and_19_out, wreg19, RegWEn);
  and and_20 (and_20_out, wreg20, RegWEn);
  and and_21 (and_21_out, wreg21, RegWEn);
  and and_22 (and_22_out, wreg22, RegWEn);
  and and_23 (and_23_out, wreg23, RegWEn);
  and and_24 (and_24_out, wreg24, RegWEn);
  and and_25 (and_25_out, wreg25, RegWEn);
  and and_26 (and_26_out, wreg26, RegWEn);
  and and_27 (and_27_out, wreg27, RegWEn);
  and and_28 (and_28_out, wreg28, RegWEn);
  and and_29 (and_29_out, wreg29, RegWEn);
  and and_30 (and_30_out, wreg30, RegWEn);
  and and_31 (and_31_out, wreg31, RegWEn);
  Register #(.width(32)) register_1 (.D(undriven), .en(and_1_out), .clk(clk), .Q(ra));  // open: clr
  Register #(.width(32)) register_2 (.D(undriven), .en(and_2_out), .clk(clk), .Q(sp));  // open: clr
  Register #(.width(32)) register_3 (.D(undriven), .en(and_3_out), .clk(clk), .Q(rg4));  // open: clr
  Register #(.width(32)) register_4 (.D(undriven), .en(and_4_out), .clk(clk), .Q(rg5));  // open: clr
  Register #(.width(32)) register_5 (.D(undriven), .en(and_5_out), .clk(clk), .Q(t0));  // open: clr
  Register #(.width(32)) register_6 (.D(undriven), .en(and_6_out), .clk(clk), .Q(t1));  // open: clr
  Register #(.width(32)) register_7 (.D(undriven), .en(and_7_out), .clk(clk), .Q(t2));  // open: clr
  Register #(.width(32)) register_8 (.D(undriven), .en(and_8_out), .clk(clk), .Q(s0));  // open: clr
  Register #(.width(32)) register_9 (.D(undriven), .en(and_9_out), .clk(clk), .Q(s1));  // open: clr
  Register #(.width(32)) register_10 (.D(undriven), .en(and_10_out), .clk(clk), .Q(a0));  // open: clr
  Register #(.width(32)) register_11 (.D(undriven), .en(and_11_out), .clk(clk), .Q(rg12));  // open: clr
  Register #(.width(32)) register_12 (.D(undriven), .en(and_12_out), .clk(clk), .Q(rg13));  // open: clr
  Register #(.width(32)) register_13 (.D(undriven), .en(and_13_out), .clk(clk), .Q(rg14));  // open: clr
  Register #(.width(32)) register_14 (.D(undriven), .en(and_14_out), .clk(clk), .Q(rg15));  // open: clr
  Register #(.width(32)) register_15 (.D(undriven), .en(and_15_out), .clk(clk), .Q(rg16));  // open: clr
  Register #(.width(32)) register_16 (.D(undriven), .en(and_16_out), .clk(clk), .Q(rg17));  // open: clr
  Register #(.width(32)) register_17 (.D(undriven), .en(and_17_out), .clk(clk), .Q(rg18));  // open: clr
  Register #(.width(32)) register_18 (.D(undriven), .en(and_18_out), .clk(clk), .Q(rg19));  // open: clr
  Register #(.width(32)) register_19 (.D(undriven), .en(and_19_out), .clk(clk), .Q(rg20));  // open: clr
  Register #(.width(32)) register_20 (.D(undriven), .en(and_20_out), .clk(clk), .Q(rg21));  // open: clr
  Register #(.width(32)) register_21 (.D(undriven), .en(and_21_out), .clk(clk), .Q(rg22));  // open: clr
  Register #(.width(32)) register_22 (.D(undriven), .en(and_22_out), .clk(clk), .Q(rg23));  // open: clr
  Register #(.width(32)) register_23 (.D(undriven), .en(and_23_out), .clk(clk), .Q(rg24));  // open: clr
  Register #(.width(32)) register_24 (.D(undriven), .en(and_24_out), .clk(clk), .Q(rg25));  // open: clr
  Register #(.width(32)) register_25 (.D(undriven), .en(and_25_out), .clk(clk), .Q(rg26));  // open: clr
  Register #(.width(32)) register_26 (.D(undriven), .en(and_26_out), .clk(clk), .Q(rg27));  // open: clr
  Register #(.width(32)) register_27 (.D(undriven), .en(and_27_out), .clk(clk), .Q(rg28));  // open: clr
  Register #(.width(32)) register_28 (.D(undriven), .en(and_28_out), .clk(clk), .Q(rg29));  // open: clr
  Register #(.width(32)) register_29 (.D(undriven), .en(and_29_out), .clk(clk), .Q(rg30));  // open: clr
  Register #(.width(32)) register_30 (.D(undriven), .en(and_30_out), .clk(clk), .Q(rg31));  // open: clr
  Register #(.width(32)) register_31 (.D(undriven), .clk(clk), .Q(rg32));  // open: en, clr
  Multiplexer #(.enable("false"), .select(5), .width(32)) multiplexer_1 (
    .in0({32{1'b0}}), .in1(ra), .in2(sp), .in3(rg4), .in4(rg5), .in5(t0), .in6(t1), .in7(t2), .in8(s0),
    .in9(s1), .in10(a0), .in11(rg12), .in12(rg13), .in13(rg14), .in14(rg15), .in15(rg16), .in16(rg17),
    .in17(rg18), .in18(rg19), .in19(rg20), .in20(rg21), .in21(rg22), .in22(rg23), .in23(rg24), .in24(rg25),
    .in25(rg26), .in26(rg27), .in27(rg28), .in28(rg29), .in29(rg30), .in30(rg31), .in31(rg32),
    .out(Read_Data_1), .sel(rs1));
  Multiplexer #(.enable("false"), .select(5), .width(32)) multiplexer_2 (
    .in0({32{1'b0}}), .in1(ra), .in2(sp), .in3(rg4), .in4(rg5), .in5(t0), .in6(t1), .in7(t2), .in8(s0),
    .in9(s1), .in10(a0), .in11(rg12), .in12(rg13), .in13(rg14), .in14(rg15), .in15(rg16), .in16(rg17),
    .in17(rg18), .in18(rg19), .in19(rg20), .in20(rg21), .in21(rg22), .in22(rg23), .in23(rg24), .in24(rg25),
    .in25(rg26), .in26(rg27), .in27(rg28), .in28(rg29), .in29(rg30), .in30(rg31), .in31(rg32),
    .out(Read_Data_2), .sel(rs2));

  // Other names for the same wires on the sheet: read_data1[31:0] = Read_Data_1; read_data2[31:0] = Read_Data_2;
  //   read_reg1[4:0] = rs1; read_reg2[4:0] = rs2; rg2[31:0] = ra; rg3[31:0] = sp; rg6[31:0] = t0; rg7[31:0] = t1;
  //   rg8[31:0] = t2; rg9[31:0] = s0; rg10[31:0] = s1; rg11[31:0] = a0; wreg12 = wreg11; write_en = RegWEn;
  //   write_reg[4:0] = rd

  // Notes on the sheet:
  //   INPUTS to your circuit
  //   DON'T CHANGE THE LOCATIONS OF THE INPUTS AND OUTPUTS!
  //   These are DEBUG/TEST outputs from your circuit.
  //   OUTPUTS from your circuit
endmodule
